# Fritzing sketch MAILBOX_notifier (saved by Fritzing 0.9.3b)

parts:
  Composant1 = Arduino MKR1000
  hc-sr2 = hc-sr04

nets:
  GND: Composant1.GND, hc-sr2.GND
  N1: Composant1.D6, hc-sr2.Trig
  N2: Composant1.D8_MOSI, hc-sr2.Echo

custom parts:
  Arduino MKR1000: MKR1000 is a powerful board that combines the functionality of the Zero and the Wi-Fi Shield. It is the ideal solution for makers wanting to design IoT projects with minimal previous experience in networking
